# Fritzing sketch wemos-blink (saved by Fritzing 0.9.3b)
breadboards: 1

parts:
  WeMos_D1_Mini1 = WeMos D1 Mini
  LED1 = smd LED [color="Red (633nm)" package="1206 [SMD]"]
  R1 = Resistor [tolerance=±5% resistance=220 package="2010 [SMD]"]

nets:
  N1: WeMos_D1_Mini1.D4, R1.Pin_0
  N2: WeMos_D1_Mini1.G, LED1.cathode
  N3: LED1.anode, R1.Pin_1
