# Fritzing sketch wemos-tof (saved by Fritzing 0.9.3b)
breadboards: 1

parts:
  WeMos_D1_Mini1 = WeMos D1 Mini
  Componente1 = GY-VL53L0XV2 Laser Ranger Module

nets:
  5V: WeMos_D1_Mini1.5V, Componente1.VCC
  N1: WeMos_D1_Mini1.D1, Componente1.SCL
  N2: WeMos_D1_Mini1.D2, Componente1.SDA
  N3: WeMos_D1_Mini1.G, Componente1.GND

custom parts:
  GY-VL53L0XV2 Laser Ranger Module: The GY-VL53L0XV2 is based on the VL53L0X from ST Microelectronics, a time-of-flight ranging system integrated into a compact module.
